// Logisim project prog.circ as structural Verilog: 15 circuits, main circuit main
module main (
  input  [2:0] in_1,
  input  in_2,
  input  [23:0] in_3,
  input  in_4,
  input  in_5,
  input  in_6,
  output out_7
);

  wire alu_1_beq, alu_1_bgt, and_1_out, and_2_out, clock, flags_E, flags_GT, isBeq, isBgt, isbranchtaken,
       isCall, isCmp, isImm, isLd, isRet, isSt, isUbranch, isWb;
  wire [2:0] multiplexer_3_out, multiplexer_4_out, multiplexer_5_out, rd, rom_1_data_3, rom_1_data_4;
  wire [4:0] rom_1_data_5;
  wire [8:0] rom_1_data;
  wire [18:9] controlunit_1_signals;
  wire [18:18] rom_1_data_2;
  wire [23:0] adder_1_out, adder_2_out, aluResult, branchPC, branchTarget, Data, immx, ldResult,
       multiplexer_1_out, multiplexer_2_out, Op2, Op_1, PC, undriven;

  of Of (
    .PC(PC), .Instruction({rom_1_data_5, rom_1_data_2[18], rd, rom_1_data_4, rom_1_data_3, rom_1_data}),
    .immx(immx), .Branch_Target(branchTarget));
  Cache cache_1 (
    .Adress({rom_1_data_4, rom_1_data_3, rom_1_data}), .Write_Data(Op2), .Clock(clock), .isStr(isSt),
    .isLd(isLd), .out_7(Data));  // open: Sel
  Register #(.width(24)) register_1 (.D(undriven), .en(in_4), .Q(PC), .clk(clock), .clr(in_5));
  Adder #(.width(24)) adder_1 (.a(in_3), .b(PC), .out(adder_1_out), .cin(in_2), .cout(out_7));
  Demultiplexer #(.width(24), .enable("false")) demultiplexer_1 (
    .out0(adder_1_out), .out1(branchPC), .in(undriven), .sel(isbranchtaken));
  Multiplexer #(.width(24), .enable("false")) multiplexer_1 (
    .in0(Op2), .in1(immx), .out(multiplexer_1_out), .sel(isImm));
  ROM #(.addrWidth(24), .dataWidth(24)) rom_1 (
    .addr(PC), .data({rom_1_data_5, rom_1_data_2[18], rd, rom_1_data_4, rom_1_data_3, rom_1_data}));  // open: sel
  Adder #(.width(24)) adder_2 (.a(PC), .b(24'h4), .out(adder_2_out));  // open: cin, cout
  Multiplexer #(.select(2), .width(24)) multiplexer_2 (
    .in0(aluResult), .in1(ldResult), .in2(adder_2_out), .out(multiplexer_2_out), .sel({isCall, isLd}));  // open: in3, en
  Multiplexer #(.width(3), .enable("false")) multiplexer_3 (
    .in0(rom_1_data_4), .in1(in_1), .out(multiplexer_3_out), .sel(isRet));
  Multiplexer #(.width(3), .enable("false")) multiplexer_4 (
    .in0(rom_1_data_3), .in1(rd), .out(multiplexer_4_out), .sel(isSt));
  Clock clock_1 (.out(clock));
  alu alu_1 (
    .in_1({controlunit_1_signals[18:12], isCmp, controlunit_1_signals[10:9], isCall, isUbranch, isWb, isImm, isRet, isBgt, isBeq, isLd, isSt}),
    .A(Op_1), .B(multiplexer_1_out), .out_4(aluResult), .Bgt(alu_1_bgt), .Beq(alu_1_beq));
  controlunit controlunit_1 (
    .opcode(rom_1_data_5), .imm(rom_1_data_2[18]),
    .signals({controlunit_1_signals[18:12], isCmp, controlunit_1_signals[10:9], isCall, isUbranch, isWb, isImm, isRet, isBgt, isBeq, isLd, isSt}));
  Multiplexer #(.width(3)) multiplexer_5 (.in0(rd), .in1(3'b111), .out(multiplexer_5_out), .en(isCall));  // open: sel
  registerbank registerbank_1 (
    .read_register_1(multiplexer_3_out), .read_register_2(multiplexer_4_out),
    .write_Register(multiplexer_5_out), .in_4(multiplexer_2_out), .in_5(isWb), .read_data_1(Op_1),
    .out_8(Op2), .Clock(clock));
  // Flag flag_1: pin names not known; wires that end beside it: isCmp, alu_1_bgt, alu_1_beq, flags_GT, flags_E
  and and_1 (and_1_out, isBeq, flags_E);
  and and_2 (and_2_out, isBgt, flags_GT);
  or or_1 (isbranchtaken, isUbranch, and_1_out, and_2_out);
  Multiplexer #(.width(24), .enable("false")) multiplexer_6 (
    .in0(branchTarget), .in1(Op_1), .out(branchPC), .sel(isRet));
  Hex_Digit_Display hex_digit_display_1 (.value(Op_1[3:0]));  // open: dp
  Hex_Digit_Display hex_digit_display_2 (.value(Op_1[7:4]));  // open: dp
  Hex_Digit_Display hex_digit_display_3 (.value(Op_1[11:8]));  // open: dp
  Hex_Digit_Display hex_digit_display_4 (.value(Op_1[15:12]));  // open: dp
  Hex_Digit_Display hex_digit_display_5 (.value(Op_1[19:16]));  // open: dp
  Hex_Digit_Display hex_digit_display_6 (.value(Op_1[23:20]));  // open: dp

  // Notes on the sheet:
  //   contents of rom_1 (hex, n*v repeats v):
  //   0 230a 304 c43 c000a ba00 4b00 4c c4a0 bc 4a0c 430c f04 d90
endmodule

// register file
module registerbank (
  input  [2:0] read_register_1,
  input  [2:0] read_register_2,
  input  [2:0] write_Register,
  input  [23:0] in_4,
  input  in_5,
  input  Clock,
  output [23:0] read_data_1,
  output [23:0] out_8
);

  wire and_1_out, and_2_out, and_3_out, and_4_out, and_5_out, and_6_out, and_7_out, and_8_out,
       decoder_1_out0, decoder_1_out1, decoder_1_out2, decoder_1_out3, decoder_1_out4, decoder_1_out5,
       decoder_1_out6, decoder_1_out7;
  wire [23:0] register_1_q, register_2_q, register_3_q, register_4_q, register_5_q, register_6_q,
       register_7_q, register_8_q;

  Decoder #(.select(3)) decoder_1 (
    .out0(decoder_1_out0), .out1(decoder_1_out1), .out2(decoder_1_out2), .out3(decoder_1_out3),
    .out4(decoder_1_out4), .out5(decoder_1_out5), .out6(decoder_1_out6), .out7(decoder_1_out7),
    .sel(write_Register));  // open: en
  and and_1 (and_1_out, decoder_1_out0, in_5, Clock);
  and and_2 (and_2_out, decoder_1_out1, in_5, Clock);
  and and_3 (and_3_out, decoder_1_out2, in_5, Clock);
  and and_4 (and_4_out, decoder_1_out3, in_5, Clock);
  and and_5 (and_5_out, decoder_1_out4, in_5, Clock);
  and and_6 (and_6_out, decoder_1_out5, in_5, Clock);
  and and_7 (and_7_out, decoder_1_out6, in_5, Clock);
  and and_8 (and_8_out, decoder_1_out7, in_5, Clock);
  Register #(.width(24), .trigger("falling")) register_1 (
    .D(in_4), .Q(register_1_q), .clk(and_1_out));  // open: en, clr
  Register #(.width(24), .trigger("falling")) register_2 (
    .D(in_4), .Q(register_2_q), .clk(and_2_out));  // open: en, clr
  Register #(.width(24), .trigger("falling")) register_3 (
    .D(in_4), .Q(register_3_q), .clk(and_3_out));  // open: en, clr
  Register #(.width(24), .trigger("falling")) register_4 (
    .D(in_4), .Q(register_4_q), .clk(and_4_out));  // open: en, clr
  Register #(.width(24), .trigger("falling")) register_5 (
    .D(in_4), .Q(register_5_q), .clk(and_5_out));  // open: en, clr
  Register #(.width(24), .trigger("falling")) register_6 (
    .D(in_4), .Q(register_6_q), .clk(and_6_out));  // open: en, clr
  Register #(.width(24), .trigger("falling")) register_7 (
    .D(in_4), .Q(register_7_q), .clk(and_7_out));  // open: en, clr
  Register #(.width(24), .trigger("falling")) register_8 (
    .D(in_4), .Q(register_8_q), .clk(and_8_out));  // open: en, clr
  Multiplexer #(.select(3), .width(24)) multiplexer_1 (
    .in0(register_1_q), .in1(register_2_q), .in2(register_3_q), .in3(register_4_q), .in4(register_5_q),
    .in5(register_6_q), .in6(register_7_q), .in7(register_8_q), .out(read_data_1), .sel(read_register_1));  // open: en
  Multiplexer #(.select(3), .width(24)) multiplexer_2 (
    .in1(register_1_q), .in2(register_2_q), .in3(register_3_q), .in4(register_4_q), .in5(register_5_q),
    .in6(register_6_q), .in7(register_7_q), .out(out_8), .sel(read_register_2));  // open: in0, en
endmodule

// CU
module controlunit (
  input  [4:0] opcode,
  input  imm,
  output [18:0] signals
);

  wire and_1_out, and_2_out, and_3_out, and_4_out, and_5_out, and_6_out, not_1_out, not_2_out, not_3_out,
       not_4_out, not_5_out, not_6_out, or_1_out, or_2_out, or_3_out;

  not not_1 (not_1_out, opcode[4]);
  not not_2 (not_2_out, opcode[0]);
  not not_3 (not_3_out, opcode[1]);
  not not_4 (not_4_out, opcode[2]);
  not not_5 (not_5_out, opcode[3]);
  and isSt (signals[0], opcode[0], opcode[1], opcode[2], opcode[3], not_1_out);
  and isLd (signals[1], not_2_out, opcode[1], opcode[2], opcode[3], not_1_out);
  and isBeq (signals[2], not_2_out, not_3_out, not_4_out, not_5_out, opcode[4]);
  and isBgt (signals[3], opcode[0], not_2_out, not_3_out, not_4_out, opcode[4]);
  and isRet (signals[4], not_2_out, not_3_out, opcode[2], not_5_out, opcode[4]);
  and and_1 (and_1_out, opcode[0], opcode[1], not_4_out, not_5_out, opcode[4]);
  or or_1 (or_1_out, not_3_out, opcode[3]);
  and and_2 (and_2_out, not_2_out, not_3_out, opcode[3]);
  and and_3 (and_3_out, not_4_out, opcode[1]);
  and isCall (signals[8], opcode[0], opcode[1], not_4_out, not_5_out, opcode[4]);
  and and_4 (and_4_out, not_2_out, not_3_out, not_4_out, not_5_out, not_1_out);
  and and_5 (and_5_out, opcode[1], opcode[2], opcode[3], not_1_out);
  and isSub (signals[10], opcode[0], not_3_out, not_4_out, not_5_out, not_1_out);
  and isCmp (signals[11], opcode[0], not_3_out, opcode[2], not_5_out, not_1_out);
  and isLsl (signals[12], not_2_out, opcode[1], not_4_out, opcode[3], not_1_out);
  and isLsr (signals[13], opcode[0], opcode[1], not_4_out, opcode[3], not_1_out);
  and isAsr (signals[14], not_2_out, not_3_out, opcode[2], opcode[3], not_1_out);
  and isOr (signals[15], opcode[0], opcode[1], opcode[2], not_5_out, not_1_out);
  and isAnd (signals[16], not_2_out, opcode[1], opcode[2], not_5_out, not_1_out);
  and isNot (signals[17], not_2_out, not_3_out, not_4_out, opcode[3], not_1_out);
  and isMov (signals[18], opcode[0], not_3_out, not_4_out, opcode[3], not_1_out);
  and and_6 (and_6_out, or_1_out, opcode[0], opcode[2], not_1_out);
  or or_2 (or_2_out, and_2_out, and_3_out);
  or isAdd (signals[9], and_4_out, and_5_out);
  or isWb (signals[6], and_1_out, not_6_out);
  or or_3 (or_3_out, and_6_out, opcode[4]);
  not not_6 (not_6_out, or_3_out);
  and isUbranch (signals[7], or_2_out, not_5_out, opcode[4]);

  assign signals[5] = imm;
endmodule

// Memory
module ma (
  input  [14:0] Address,
  input  [23:0] in_2,
  input  clock,
  input  isLoad,
  input  isStore,
  output [23:0] out_6
);

  wire and_1_out, or_1_out;

  and and_1 (and_1_out, clock, or_1_out);
  or or_1 (or_1_out, isStore, isLoad);
  RAM #(.addrWidth(15), .dataWidth(24), .bus("separate")) ram_1 (
    .addr(Address), .din(in_2), .data(out_6), .str(isStore), .clk(and_1_out), .ld(isLoad));  // open: sel, clr
endmodule

module RW_cicuit (
  input  [2:0] Write_port,
  input  [2:0] Read_port_1,
  input  [2:0] Read_port_2,
  input  [2:0] rd_23_26,
  input  [2:0] ra,
  input  isCall,
  input  [23:0] aluResult,
  input  isWb,
  input  [23:0] ldResult,
  input  [23:0] Write_data,
  input  [23:0] pc_offset,
  input  [23:0] in_12,
  input  isLd,
  input  isCall_2,
  output [23:0] read_port_1_data,
  output [23:0] read_port_2_data
);

  wire clock_1_out;
  wire [23:0] adder_1_out;

  Adder #(.width(24)) adder_1 (.a(pc_offset), .b(in_12), .out(adder_1_out));  // open: cin, cout
  Multiplexer #(.width(3)) multiplexer_1 (.in0(rd_23_26), .in1(ra), .out(Write_port), .sel(isCall));  // open: en
  registerbank registerbank_1 ();  // open: read_register_1, read_register_2, write_Register, in_4, in_5, read_data_1, out_8, Clock
  Clock clock_1 (.out(clock_1_out));
  Multiplexer #(.select(2), .width(24)) multiplexer_2 (
    .in0(aluResult), .in1(ldResult), .in2(adder_1_out), .out(Write_data), .sel({isCall_2, isLd}));  // open: in3, en
endmodule

module of (
  input  [23:0] PC,
  input  [23:0] Instruction,
  output [23:0] immx,
  output [23:0] Branch_Target
);

  calc_immx Immediate_Calculator (.Immediate_Bits(Instruction[11:0]), .Extended_Immediate(immx));
  Adder #(.width(24)) adder_1 (
    .a(PC), .b({{5{Instruction[17]}}, Instruction[16:0], 2'b00}), .out(Branch_Target));  // open: cin, cout
endmodule

module calc_immx (
  input  [11:0] Immediate_Bits,
  output [23:0] Extended_Immediate
);

  Multiplexer #(.select(2), .width(24), .enable("false")) multiplexer_1 (
    .in0({{15{Immediate_Bits[9]}}, Immediate_Bits[8:0]}), .in1({{14{1'b0}}, Immediate_Bits[9:0]}),
    .in2({Immediate_Bits[9:0], {14{1'b0}}}), .out(Extended_Immediate), .sel(Immediate_Bits[11:10]));  // open: in3
endmodule

// Cache and Memory
module Cache (
  input  [14:0] Adress,
  input  [23:0] Write_Data,
  input  Sel,
  input  Clock,
  input  isLd,
  input  isStr,
  output [23:0] out_7
);

  wire and_1_out, Hit, not_1_out;
  wire [3:0] index, tag_adress_1_index;
  wire [23:0] Data;

  Tag_Adress tag_adress_1 (.in_2(Adress), .index(tag_adress_1_index), .Hit_Miss(Hit));  // open: in_1, in_3, in_4
  not not_1 (not_1_out, Hit);
  assign index = Hit ? tag_adress_1_index : 4'bz;  // Controlled_Buffer controlled_buffer_1
  Block_Adress block_adress_1 (
    .in_2(Write_Data), .in_3(Sel), .in_4(Clock), .in_1(index), .in_6(and_1_out), .in_5(isLd), .out_7(Data));
  and and_1 (and_1_out, not_1_out, isStr);
  ma ma_1 (.Address(Adress), .in_2(Write_Data), .clock(Clock), .isStore(isStr), .isLoad(isLd), .out_6(out_7));
endmodule

module Tag_Adress (
  input  in_1,
  input  [14:0] in_2,
  input  in_3,
  input  in_4,
  output [3:0] index,
  output Hit_Miss
);

  wire [5:0] ram_1_data;

  RAM #(.addrWidth(4), .dataWidth(6), .bus("separate")) ram_1 (
    .addr(in_2[9:6]), .data(ram_1_data), .str(in_1), .sel(in_3), .ld(in_4));  // open: din, clk, clr
  Comparator #(.width(6)) comparator_1 (
    .a(ram_1_data), .b({in_2[0], in_2[1], in_2[2], in_2[3], in_2[4], in_2[5]}), .eq(Hit_Miss));  // open: gt, lt

  assign index = in_2[9:6];

  // Other names for the same wires on the sheet: Tag[5:0] = {in_2[0], in_2[1], in_2[2], in_2[3], in_2[4], in_2[5]}
endmodule

module Block_Adress (
  input  [3:0] in_1,
  input  [23:0] in_2,
  input  in_3,
  input  in_4,
  input  in_5,
  input  in_6,
  output [23:0] out_7
);

  RAM #(.addrWidth(4), .dataWidth(24), .bus("separate")) ram_1 (
    .addr(in_1), .din(in_2), .data(out_7), .str(in_6), .sel(in_3), .clk(in_4), .ld(in_5));  // open: clr
endmodule

module \logic  (
  input  [23:0] A,
  input  [23:0] B,
  input  IsAND,
  input  IsOR,
  input  IsXOR,
  input  IsMOV,
  output [23:0] out_7
);

  wire or_4_out;
  wire [1:0] or_2_out;
  wire [23:0] and_1_out, or_1_out, xor_1_out;

  assign and_1_out = A & B;  // AND_Gate and_1, 24 bits wide
  assign or_1_out = A | B;  // OR_Gate or_1, 24 bits wide
  assign xor_1_out = A ^ B;  // XOR_Gate xor_1, 24 bits wide
  or or_2 (or_2_out[0], IsMOV, IsOR);
  or or_3 (or_2_out[1], IsXOR, IsMOV);
  Multiplexer #(.select(2), .width(24)) multiplexer_1 (
    .in0(and_1_out), .in1(or_1_out), .in2(xor_1_out), .in3(B), .out(out_7), .sel(or_2_out), .en(or_4_out));
  or or_4 (or_4_out, IsAND, IsOR, IsXOR, IsMOV);
endmodule

module shift (
  input  [23:0] A,
  input  [23:0] B,
  input  IsLSL,
  input  IsLSR,
  input  IsASR,
  output [23:0] out_6
);

  wire or_3_out;
  wire [1:0] or_1_out;
  wire [4:0] bit_extender_1_out;
  wire [23:0] shifter_1_out, shifter_2_out, shifter_3_out;

  Bit_Extender #(.in_width(24), .out_width(5)) bit_extender_1 (.in(B), .out(bit_extender_1_out));
  Shifter #(.width(24), .shift("lr")) shifter_1 (.in(A), .\dist (bit_extender_1_out), .out(shifter_1_out));
  Shifter #(.width(24), .shift("ar")) shifter_2 (.in(A), .\dist (bit_extender_1_out), .out(shifter_2_out));
  Shifter #(.width(24)) shifter_3 (.in(A), .\dist (bit_extender_1_out), .out(shifter_3_out));
  or or_1 (or_1_out[0], IsLSL, IsLSR);
  or or_2 (or_1_out[1], IsLSL, IsASR);
  or or_3 (or_3_out, IsLSL, IsLSR, IsASR);
  Multiplexer #(.select(2), .width(24)) multiplexer_1 (
    .in1(shifter_1_out), .in2(shifter_2_out), .in3(shifter_3_out), .out(out_6), .sel(or_1_out), .en(or_3_out));  // open: in0

  // Notes on the sheet:
  //   LSR
  //   ASR
  //   LSL
endmodule

module alu (
  input  [18:0] in_1,
  input  [23:0] A,
  input  [23:0] B,
  output [23:0] out_4,
  output Bgt,
  output Beq
);

  wire or_1_out, or_2_out, or_3_out;
  wire [1:0] or_4_out;
  wire [23:0] arithmetic_1_out_4, logic_1_out_7, shift_1_out_6;

  or or_1 (or_1_out, in_1[18], in_1[17], in_1[16], in_1[15]);
  or or_2 (or_2_out, in_1[11], in_1[10], in_1[9]);
  or or_3 (or_3_out, in_1[14], in_1[13], in_1[12]);
  \logic  logic_1 (
    .A(A), .B(B), .IsAND(in_1[16]), .IsOR(in_1[15]), .IsXOR(in_1[17]), .IsMOV(in_1[18]), .out_7(logic_1_out_7));
  shift shift_1 (.A(A), .B(B), .IsLSL(in_1[12]), .IsLSR(in_1[13]), .IsASR(in_1[14]), .out_6(shift_1_out_6));
  arithmetic arithmetic_1 (.A(A), .B(B), .IsSub(in_1[10]), .out_4(arithmetic_1_out_4), .Bgt(Bgt), .Beq(Beq));
  or or_4 (or_4_out[0], or_2_out, or_1_out);
  or or_5 (or_4_out[1], or_3_out, or_2_out);
  Multiplexer #(.select(2), .width(24)) multiplexer_1 (
    .in0({24{1'b0}}), .in1(logic_1_out_7), .in2(shift_1_out_6), .in3(arithmetic_1_out_4), .out(out_4),
    .sel(or_4_out), .en(1'b1));
endmodule

module arithmetic (
  input  [23:0] A,
  input  [23:0] B,
  input  IsSub,
  output [23:0] out_4,
  output Bgt,
  output Beq
);

  wire [23:0] adder_1_out, adder_2_out;

  Adder #(.width(24)) adder_1 (.a(A), .b(B), .out(adder_1_out));  // open: cin, cout
  Adder #(.width(24)) adder_2 (.a(A), .b(B), .out(adder_2_out));  // open: cin, cout
  Comparator #(.width(24)) comparator_1 (.a(A), .b(B), .gt(Bgt), .eq(Beq));  // open: lt
  Multiplexer #(.width(24)) multiplexer_1 (.in0(adder_1_out), .in1(adder_2_out), .out(out_4), .sel(IsSub), .en(1'b1));
endmodule

module flag (
  input  isCmp,
  input  bgt,
  input  beq,
  output flags_GT,
  output flags_E
);

  D_Flip_Flop #(.trigger("high")) d_ff_1 (.clk(isCmp), .D(bgt), .Q(flags_GT));  // open: Qn, preset, en, reset
  D_Flip_Flop #(.trigger("high")) d_ff_2 (.clk(isCmp), .D(beq), .Q(flags_E));  // open: Qn, preset, en, reset
endmodule
